# Fritzing sketch Layout (saved by Fritzing 0.9.3b)

parts:
  U1 = NodeMCU V1.0
  R1 = Resistor [tolerance=±5% resistance=470 package="0805 [SMD]"]
  DS1 = DS18B20 1-Wire Temperature Sensor [part_number=DS18B20]
  J1 = Camdenboss CTB0158-3 [part_number=CTB0158-3 package=THT]
  LED1 = RGB LED (com. cathode, rbg) [package="5 mm [THT]"]

nets:
  N1: U1.D4, LED1.red_anode
  N2: U1.GND, R1.Pin_1, J1.pin2, LED1.common_cathode
  N3: U1.D5, LED1.blue_anode
  N4: U1.D6, LED1.green_anode
  N5: U1.D8, R1.Pin_0, J1.pin1
  N6: U1.3V3, J1.pin3
  N7: DS1.VDD, J1.terminal_3
  N8: DS1.DQ, J1.terminal_2
  N9: DS1.GND, J1.terminal_1

custom parts:
  NodeMCU V1.0: ESP8266 based NodeMCU
